# Fritzing sketch schaltplan (saved by Fritzing 0.9.5d)
breadboards: 1

parts:
  Raspberry_Pi_1 = Raspberry Pi 3 [part_number=RPI-3-V1.2]
  Part1 = RFID-RC522-v3
  M1 = DC Motor
  LED1 = LED - 5mm [color="Red (633nm)" package="5 mm [THT]"]
  R1 = Resistor [tolerance=±5% resistance=220 package=THT]
  Mod1 = KY-019 5V Relay Module [package="Breakout board"]

nets:
  3V3: Raspberry_Pi_1.3v3, Part1.3.3V
  N1: Raspberry_Pi_1.GPIO2, Mod1.S
  N2: Raspberry_Pi_1.GPIO3, R1.Pin_0
  N3: Raspberry_Pi_1.GIPO10, Part1.MOSI
  N4: Raspberry_Pi_1.GIPO9, Part1.MISO
  N5: Raspberry_Pi_1.GIPO11, Part1.SCK
  N6: Raspberry_Pi_1.GIPO8, Part1.SDA
  N7: Raspberry_Pi_1.GIPO25, Part1.RST
  GND: Raspberry_Pi_1.GND, Part1.GND, LED1.anode, Mod1.-
  N8: Raspberry_Pi_1.5V, Mod1.+
  N9: M1.pin_1, Mod1.NC
  N10: LED1.cathode, R1.Pin_1

custom parts:
  RFID-RC522-v3: A simple China made RFID-RC522 Reader (6x4 cm); do check the pin labels, as this is a MFRC522 based clone.
  KY-019 5V Relay Module: KY-019 5V Relay module, used to control AC circuits. (Special thanks to vanepp for fixing the PCB holes and other errors)
